# Fritzing sketch car_veroboard_sketch (saved by Fritzing 0.9.3b)
circuit board: 10cm x 6.5cm
perfboards: 1

parts:
  Part1 = Arduino Nano (Rev3.0) (ICSP)
  J1 = female pin header, 2 pins [form="♀ (female)"]
  J2 = female pin header, 2 pins [form="♀ (female)"]
  J3 = female pin header, 2 pins [form="♀ (female)"]
  J4 = female pin header, 2 pins [form="♀ (female)"]
  IC1 = L293D [package=THT]
  J5 = female pin header, 2 pins [form="♀ (female)"]
  J6 = Camdenboss CTB0158-2 [part_number=CTB0158-2 package=THT]
  J7 = Camdenboss CTB0158-2 [part_number=CTB0158-2 package=THT]
  J8 = Camdenboss CTB0158-2 [part_number=CTB0158-2 package=THT]
  IC2 = Voltage Regulator [package=to220-igo]
  JP1 = Header 3 [package=screwterminal-3.5mm-3_lock.007s]
  JP2 = Header 3 [package=screwterminal-3.5mm-3_lock.007s]

nets (from the pcb view):
  GND: Part1.GND, J1.pin2, J3.pin1, IC1.0V, J6.pin1, IC2.GND, JP1.3, JP2.3
  N1: Part1.D2, J2.pin2
  N2: Part1.D3, J2.pin1
  N3: Part1.D4, J5.pin1
  N4: Part1.D5, J3.pin2
  N5: Part1.D6, JP1.1
  N6: Part1.D7, JP2.1
  N7: Part1.D10, J4.pin1
  N8: Part1.D11/MOSI, J4.pin2
  N9: Part1.D12/MISO, IC1.In_2
  N10: Part1.VIN, J1.pin1, J5.pin2, IC2.OUT, JP1.2, JP2.2
  N11: Part1.5V, IC1.+V
  N12: Part1.A3, IC1.In_1
  N13: Part1.A2, IC1.Enable_1
  N14: Part1.A1, IC1.Enable_2
  N15: Part1.A0, IC1.In_3
  N16: Part1.D13/SCK, IC1.In_4
  N17: IC1.Out_1_(_Controlled_by_Enable_1_), J8.pin1
  N18: IC1.Out_2_(_Controlled_by_Enable_1_), J8.pin2
  N19: IC1.+Vmotor, J6.pin2, IC2.IN
  N20: IC1.Out_3_(_Controlled_by_Enable_2_), J7.pin1
  N21: IC1.Out_4_(_Controlled_by_Enable_2_), J7.pin2
